# Fritzing sketch SmartPillow (saved by Fritzing 0.9.3b)
breadboards: 1

parts:
  Part1 = Arduino Uno (Rev3)
  Part2 = Bluetooth HC-05 Macho
  ZS-042_RTC1 = ZS-042 RTC Module
  J1 = Basic Force Sensing Resistor (FSR) [package=THT]
  U1 = Vibration Motor- ROB-08449 [package=vibe-motor-10mm]
  S2 = Pushbutton [package="[THT]"]
  J2 = Basic Force Sensing Resistor (FSR) [package=THT]
  U2 = Vibration Motor- ROB-08449 [package=vibe-motor-10mm]
  LED1 = smd LED [color="Green (570nm)" package="1206 [SMD]"]
  LED2 = LED - 5mm [color="Red (633nm)" package="5 mm [THT]"]
  R1 = Resistor [tolerance=±5% resistance=220 package=THT]
  R2 = Resistor [tolerance=±5% resistance=220 package=THT]
  Q1 = Basic FET P-Channel [package="TO220 [THT]"]
  U3 = LIPO-1000mAh [package=lipo-1000]
  Q2 = Basic FET P-Channel [package="TO220 [THT]"]

nets:
  N1: Part1.A2, J1.pin_0
  N2: Part1.A4/SDA, ZS-042_RTC1.SDA
  N3: Part1.A5/SCL, ZS-042_RTC1.SCL
  N4: Part1.D8, Part2.VCC
  N5: Part1.D10_PWM/SS, Q2.gate
  N6: Part1.D11_PWM/MOSI, Q1.gate
  N7: Part1.D2, ZS-042_RTC1.SQW
  N8: Part1.D4, Part2.TXD
  N9: Part1.D7, S2.Pin_1, S2.Pin_2
  5V: Part1.5V, ZS-042_RTC1.VCC, J1.pin_1, S2.Pin_3, S2.Pin_4, J2.pin_1, R1.Pin_0
  GND: Part1.GND, Part2.GND, ZS-042_RTC1.GND, R1.Pin_1, Q1.source, U3.-, Q2.source
  N10: Part1.VIN, U1.-, U2.-, R2.Pin_1, U3.+
  N11: U1.+, U2.+, Q1.drain
  N12: LED1.cathode, LED2.cathode, Q2.drain
  N13: LED1.anode, LED2.anode, R2.Pin_0
